# Fritzing sketch nodo_acel (saved by Fritzing 0.9.4)
breadboards: 1

parts:
  NodeMCU_(Amica) = Amica NodeMCU DEVKIT 1.0
  C1 = Electrolytic Capacitor [capacitance=220µF voltage=16V package="200 mil [THT, electrolytic]"]
  R5 = Resistor [resistance=330Ω package=THT]
  R6 = Resistor [resistance=330Ω package=THT]
  ADS1115 = Adafruit ADS1115 16Bit I2C ADC
  GY61 = GY-61 (ADXL335)
  LED_V = LED - 5mm [color="Green (570nm)" package="5 mm [THT]"]
  LED_R = LED - 5mm [color="Red (633nm)" package="5 mm [THT]"]

nets:
  3V3: NodeMCU_(Amica).pin1, NodeMCU_(Amica).pin_10, NodeMCU_(Amica).pin_26, ADS1115.VDD, GY61.VCC
  GND: NodeMCU_(Amica).pin2, NodeMCU_(Amica).pin_9, NodeMCU_(Amica).pin_25, NodeMCU_(Amica).pin_29, C1.-, ADS1115.ADDR, ADS1115.GND, GY61.GND, LED_V.cathode, LED_R.cathode
  D8: NodeMCU_(Amica).pin5, R6.Pin_0
  D7: NodeMCU_(Amica).pin6, R5.Pin_0
  SDA: NodeMCU_(Amica).pin_13, ADS1115.SDA
  SCL: NodeMCU_(Amica).pin_14, ADS1115.SCL
  5V: NodeMCU_(Amica).pin_30, C1.+
  LED_V: R5.Pin_1, LED_V.anode
  LED_R: R6.Pin_1, LED_R.anode
  Z: ADS1115.AIN2, GY61.Z
  Y: ADS1115.AIN1, GY61.Y
  X: ADS1115.AIN0, GY61.X

custom parts:
  Adafruit ADS1115 16Bit I2C ADC: For microcontrollers without an analog-to-digital converter or when you want a higher-precision ADC, the ADS1115 provides 16-bit precision at 860 samples/second over I2C. The chip can be configured as 4 single-ended input channels, or two differential channels. As a nice bonus, it even includes a programmable gain amplifier, up to x16, to help boost up smaller single/differential signals to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
  GY-61 (ADXL335): Acelerómetro analógico de 3 ejes GY-61 con ADXL335 (Argos, nodo acel). Orden de pines POR CONFIRMAR con la pieza real.
