# Fritzing sketch nodo_dht (saved by Fritzing 0.9.4)
breadboards: 1

parts:
  NodeMCU_(Amica) = Amica NodeMCU DEVKIT 1.0
  C1 = Electrolytic Capacitor [capacitance=220µF voltage=16V package="200 mil [THT, electrolytic]"]
  R5 = Resistor [resistance=330Ω package=THT]
  R6 = Resistor [resistance=330Ω package=THT]
  R1 = Resistor [resistance=10kΩ package=THT]
  R3 = Resistor [resistance=1kΩ package=THT]
  R4 = Resistor [resistance=10kΩ package=THT]
  Q1 = TRANSISTOR_NPN [package=to-92]
  LED_V = LED - 5mm [color="Green (570nm)" package="5 mm [THT]"]
  LED_R = LED - 5mm [color="Red (633nm)" package="5 mm [THT]"]
  Boton = Pushbutton [package=THT]
  DHT22 = DHT22 Humidity and Temperature Sensor
  Buzzer = Buzzer 12mm [package=buzzer-12mm]
  OLED = OLED 2.42" SSD1309 I²C

nets:
  3V3: NodeMCU_(Amica).pin1, NodeMCU_(Amica).pin_10, NodeMCU_(Amica).pin_26, R1.Pin_1, DHT22.VDD, OLED.VCC
  GND: NodeMCU_(Amica).pin2, NodeMCU_(Amica).pin_9, NodeMCU_(Amica).pin_25, NodeMCU_(Amica).pin_29, C1.-, R4.Pin_1, Q1.E, LED_V.cathode, LED_R.cathode, Boton.leg1, DHT22.GND, OLED.GND
  D8: NodeMCU_(Amica).pin5, R6.Pin_0
  D7: NodeMCU_(Amica).pin6, R5.Pin_0
  D6: NodeMCU_(Amica).pin7, Boton.leg0
  D5: NodeMCU_(Amica).pin8, R3.Pin_0
  DATA: NodeMCU_(Amica).pin_11, R1.Pin_0, DHT22.DATA
  SDA: NodeMCU_(Amica).pin_13, OLED.SDA
  SCL: NodeMCU_(Amica).pin_14, OLED.SCL
  5V: NodeMCU_(Amica).pin_30, C1.+, Buzzer.1
  LED_V: R5.Pin_1, LED_V.anode
  LED_R: R6.Pin_1, LED_R.anode
  BASE: R3.Pin_1, R4.Pin_0, Q1.B
  COLECTOR: Q1.C, Buzzer.2

custom parts:
  OLED 2.42" SSD1309 I²C: Pantalla OLED 2.42" 128×64 SSD1309, versión I²C de 4 pines (Argos, nodo dht). Orden de pines POR CONFIRMAR con la pieza real.
