# Fritzing sketch nodo_puerta (saved by Fritzing 0.9.4)
breadboards: 1

parts:
  NodeMCU_(Amica) = Amica NodeMCU DEVKIT 1.0
  C1 = Electrolytic Capacitor [capacitance=220µF voltage=16V package="200 mil [THT, electrolytic]"]
  R5 = Resistor [resistance=330Ω package=THT]
  R6 = Resistor [resistance=330Ω package=THT]
  LED_V = LED - 5mm [color="Green (570nm)" package="5 mm [THT]"]
  LED_R = LED - 5mm [color="Red (633nm)" package="5 mm [THT]"]
  Reed = Reed switch [package=THT]

nets:
  N1: NodeMCU_(Amica).pin1, NodeMCU_(Amica).pin_10, NodeMCU_(Amica).pin_26
  GND: NodeMCU_(Amica).pin2, NodeMCU_(Amica).pin_9, NodeMCU_(Amica).pin_25, NodeMCU_(Amica).pin_29, C1.-, LED_V.cathode, LED_R.cathode, Reed.pin_2
  D8: NodeMCU_(Amica).pin5, R6.Pin_0
  D7: NodeMCU_(Amica).pin6, R5.Pin_0
  D5: NodeMCU_(Amica).pin8, Reed.pin_1
  5V: NodeMCU_(Amica).pin_30, C1.+
  LED_V: R5.Pin_1, LED_V.anode
  LED_R: R6.Pin_1, LED_R.anode
